// Logisim project 24 bit MIPS CPU - CSE332 - Samir Mahmud - Mohaimen Al Mamun.circ as structural Verilog
module Register_File (
  input  [4:0] Read_register_1,
  input  [4:0] Write_register,
  input  [4:0] Read_register_2,
  input  [23:0] write_data,
  input  write_control,
  input  clear,
  input  Clock,
  output [23:0] Read_data_1,
  output [23:0] Read_data_2
);

  wire and_1_out, and_2_out, and_3_out, and_4_out, and_5_out, and_6_out, and_7_out, and_8_out, and_9_out,
       and_10_out, and_11_out, and_12_out, and_13_out, and_14_out, and_15_out, and_16_out, and_17_out,
       and_18_out, and_19_out, and_20_out, and_21_out, and_22_out, and_23_out, and_24_out, decoder_1_out0,
       decoder_1_out1, decoder_1_out2, decoder_1_out3, decoder_1_out4, decoder_1_out5, decoder_1_out6,
       decoder_1_out7, decoder_1_out8, decoder_1_out9, decoder_1_out10, decoder_1_out11, decoder_1_out12,
       decoder_1_out13, decoder_1_out14, decoder_1_out15, decoder_1_out16, decoder_1_out17, decoder_1_out18,
       decoder_1_out19, decoder_1_out20, decoder_1_out21, decoder_1_out22, decoder_1_out23;
  wire [23:0] _0_q, _1_q, _2_q, _3_q, _4_q, _5_q, _6_q, _7_q, _8_q, _9_q, _10_q, _11_q, _12_q, _13_q, _14_q,
       _15_q, _16_q, _17_q, _18_q, _19_q, _20_q, _21_q, _22_q, _23_q;

  Decoder #(.select(5), .enable("false")) decoder_1 (
    .out0(decoder_1_out0), .out1(decoder_1_out1), .out2(decoder_1_out2), .out3(decoder_1_out3),
    .out4(decoder_1_out4), .out5(decoder_1_out5), .out6(decoder_1_out6), .out7(decoder_1_out7),
    .out8(decoder_1_out8), .out9(decoder_1_out9), .out10(decoder_1_out10), .out11(decoder_1_out11),
    .out12(decoder_1_out12), .out13(decoder_1_out13), .out14(decoder_1_out14), .out15(decoder_1_out15),
    .out16(decoder_1_out16), .out17(decoder_1_out17), .out18(decoder_1_out18), .out19(decoder_1_out19),
    .out20(decoder_1_out20), .out21(decoder_1_out21), .out22(decoder_1_out22), .out23(decoder_1_out23),
    .sel(Write_register));  // open: out24, out25, out26, out27, out28, out29, out30, out31
  and and_1 (and_1_out, decoder_1_out0, write_control);
  and and_2 (and_2_out, decoder_1_out1, write_control);
  and and_3 (and_3_out, decoder_1_out2, write_control);
  and and_4 (and_4_out, decoder_1_out3, write_control);
  and and_5 (and_5_out, decoder_1_out4, write_control);
  and and_6 (and_6_out, decoder_1_out5, write_control);
  and and_7 (and_7_out, decoder_1_out6, write_control);
  and and_8 (and_8_out, decoder_1_out7, write_control);
  and and_9 (and_9_out, decoder_1_out8, write_control);
  and and_10 (and_10_out, decoder_1_out9, write_control);
  and and_11 (and_11_out, decoder_1_out10, write_control);
  and and_12 (and_12_out, decoder_1_out11, write_control);
  Register #(.width(24)) _0 (.D(write_data), .en(and_1_out), .Q(_0_q), .clk(Clock), .clr(clear));
  Register #(.width(24)) _1 (.D(write_data), .en(and_2_out), .Q(_1_q), .clk(Clock), .clr(clear));
  Register #(.width(24)) _2 (.D(write_data), .en(and_3_out), .Q(_2_q), .clk(Clock), .clr(clear));
  Register #(.width(24)) _3 (.D(write_data), .en(and_4_out), .Q(_3_q), .clk(Clock), .clr(clear));
  Register #(.width(24)) _4 (.D(write_data), .en(and_5_out), .Q(_4_q), .clk(Clock), .clr(clear));
  Register #(.width(24)) _5 (.D(write_data), .en(and_6_out), .Q(_5_q), .clk(Clock), .clr(clear));
  Register #(.width(24)) _6 (.D(write_data), .en(and_7_out), .Q(_6_q), .clk(Clock), .clr(clear));
  Register #(.width(24)) _7 (.D(write_data), .en(and_8_out), .Q(_7_q), .clk(Clock), .clr(clear));
  Register #(.width(24)) _8 (.D(write_data), .en(and_9_out), .Q(_8_q), .clk(Clock), .clr(clear));
  Register #(.width(24)) _9 (.D(write_data), .en(and_10_out), .Q(_9_q), .clk(Clock), .clr(clear));
  Register #(.width(24)) _10 (.D(write_data), .en(and_11_out), .Q(_10_q), .clk(Clock), .clr(clear));
  Register #(.width(24)) _11 (.D(write_data), .en(and_12_out), .Q(_11_q), .clk(Clock), .clr(clear));
  and and_13 (and_13_out, decoder_1_out12, write_control);
  and and_14 (and_14_out, decoder_1_out13, write_control);
  and and_15 (and_15_out, decoder_1_out14, write_control);
  and and_16 (and_16_out, decoder_1_out15, write_control);
  and and_17 (and_17_out, decoder_1_out16, write_control);
  and and_18 (and_18_out, decoder_1_out17, write_control);
  and and_19 (and_19_out, decoder_1_out18, write_control);
  and and_20 (and_20_out, decoder_1_out19, write_control);
  and and_21 (and_21_out, decoder_1_out20, write_control);
  and and_22 (and_22_out, decoder_1_out21, write_control);
  and and_23 (and_23_out, decoder_1_out22, write_control);
  and and_24 (and_24_out, decoder_1_out23, write_control);
  Register #(.width(24)) _12 (.D(write_data), .en(and_13_out), .Q(_12_q), .clk(Clock), .clr(clear));
  Register #(.width(24)) _13 (.D(write_data), .en(and_14_out), .Q(_13_q), .clk(Clock), .clr(clear));
  Register #(.width(24)) _14 (.D(write_data), .en(and_15_out), .Q(_14_q), .clk(Clock), .clr(clear));
  Register #(.width(24)) _15 (.D(write_data), .en(and_16_out), .Q(_15_q), .clk(Clock), .clr(clear));
  Register #(.width(24)) _16 (.D(write_data), .en(and_17_out), .Q(_16_q), .clk(Clock), .clr(clear));
  Register #(.width(24)) _17 (.D(write_data), .en(and_18_out), .Q(_17_q), .clk(Clock), .clr(clear));
  Register #(.width(24)) _18 (.D(write_data), .en(and_19_out), .Q(_18_q), .clk(Clock), .clr(clear));
  Register #(.width(24)) _19 (.D(write_data), .en(and_20_out), .Q(_19_q), .clk(Clock), .clr(clear));
  Register #(.width(24)) _20 (.D(write_data), .en(and_21_out), .Q(_20_q), .clk(Clock), .clr(clear));
  Register #(.width(24)) _21 (.D(write_data), .en(and_22_out), .Q(_21_q), .clk(Clock), .clr(clear));
  Register #(.width(24)) _22 (.D(write_data), .en(and_23_out), .Q(_22_q), .clk(Clock), .clr(clear));
  Register #(.width(24)) _23 (.D(write_data), .en(and_24_out), .Q(_23_q), .clk(Clock), .clr(clear));
  Multiplexer #(.select(5), .width(24), .enable("false")) multiplexer_1 (
    .in0(_0_q), .in1(_1_q), .in2(_2_q), .in3(_3_q), .in4(_4_q), .in5(_5_q), .in6(_6_q), .in7(_7_q),
    .in8(_8_q), .in9(_9_q), .in10(_10_q), .in11(_11_q), .in12(_12_q), .in13(_13_q), .in14(_14_q),
    .in15(_15_q), .in16(_16_q), .in17(_17_q), .in18(_18_q), .in19(_19_q), .in20(_20_q), .in21(_21_q),
    .in22(_22_q), .in23(_23_q), .out(Read_data_1), .sel(Read_register_1));  // open: in24, in25, in26, in27, in28, in29, in30, in31
  Multiplexer #(.select(5), .width(24), .enable("false")) multiplexer_2 (
    .in0(_0_q), .in1(_1_q), .in2(_2_q), .in3(_3_q), .in4(_4_q), .in5(_5_q), .in6(_6_q), .in7(_7_q),
    .in8(_8_q), .in9(_9_q), .in10(_10_q), .in11(_11_q), .in12(_12_q), .in13(_13_q), .in14(_14_q),
    .in15(_15_q), .in16(_16_q), .in17(_17_q), .in18(_18_q), .in19(_19_q), .in20(_20_q), .in21(_21_q),
    .in22(_22_q), .in23(_23_q), .out(Read_data_2), .sel(Read_register_2));  // open: in24, in25, in26, in27, in28, in29, in30, in31

  // Notes on the sheet:
  //   Figure: 24-bit Register File
endmodule

module ALU_Control_Unit (
  input  [1:0] ALUop,
  input  [3:0] Function,
  output [3:0] ALU_Control_Signal
);

  wire [3:0] multiplexer_1_out;

  Multiplexer #(.select(4), .width(4), .enable("false")) multiplexer_1 (
    .in1(4'b1000), .in2(4'b0010), .in3(4'b0001), .in4(4'b0011), .in5(4'b0100), .in6(4'b0111), .in7(4'b0101),
    .in8(4'b0110), .in9(4'b0000), .out(multiplexer_1_out), .sel(Function));  // open: in0, in10, in11, in12, in13, in14, in15
  Multiplexer #(.select(2), .width(4), .enable("false")) multiplexer_2 (
    .in0(4'b0011), .in1(4'b0110), .in2(multiplexer_1_out), .out(ALU_Control_Signal), .sel(ALUop));  // open: in3

  // Notes on the sheet:
  //   Figure: ALU Conntrol Unit
endmodule

module ALU (
  input  [23:0] Rs,
  input  [23:0] Rt,
  input  [4:0] Shampt,
  input  [3:0] ALU_control_signal,
  output [23:0] ALU_output,
  output Zero
);

  wire and_2_out, comparator_1_lt;
  wire [23:0] adder_1_out, and_1_out, bit_extender_1_out, multiplexer_1_out, nor_1_out, not_1_out, or_1_out,
       shifter_1_out, shifter_2_out;

  assign not_1_out = ~Rt;  // NOT_Gate not_1, 24 bits wide
  assign and_1_out = Rs & Rt;  // AND_Gate and_1, 24 bits wide
  assign or_1_out = Rs | Rt;  // OR_Gate or_1, 24 bits wide
  Multiplexer #(.width(24), .enable("false")) multiplexer_1 (
    .in0(Rt), .in1(not_1_out), .out(multiplexer_1_out), .sel(and_2_out));
  Comparator #(.width(24)) comparator_1 (.a(Rs), .b(Rt), .eq(Zero), .lt(comparator_1_lt));  // open: gt
  assign nor_1_out = ~(Rs | Rt);  // NOR_Gate nor_1, 24 bits wide
  Shifter #(.width(24), .shift("lr")) shifter_1 (.in(Rt), .\dist (Shampt), .out(shifter_1_out));
  Shifter #(.width(24)) shifter_2 (.in(Rt), .\dist (Shampt), .out(shifter_2_out));
  Adder #(.width(24)) adder_1 (.a(Rs), .b(multiplexer_1_out), .out(adder_1_out), .cin(and_2_out));  // open: cout
  assign bit_extender_1_out = {{23{1'b0}}, comparator_1_lt};  // Bit_Extender bit_extender_1
  and and_2 (and_2_out, ALU_control_signal[1], ALU_control_signal[2]);
  Multiplexer #(.select(4), .width(24), .enable("false")) multiplexer_2 (
    .in0(and_1_out), .in1(or_1_out), .in2(nor_1_out), .in3(adder_1_out), .in4(shifter_1_out),
    .in5(shifter_2_out), .in6(adder_1_out), .in7(bit_extender_1_out), .in8({24{1'b0}}), .out(ALU_output),
    .sel(ALU_control_signal));  // open: in9, in10, in11, in12, in13, in14, in15

  // Notes on the sheet:
  //   AND
  //   OR
  //   NOR
  //   Figure: 24-bit ALU
  //   SLT
  //   NOP
  //   Srl
  //   Sll
  //   ADD
  //   SUB
endmodule

module Main_Control_Unit (
  input  [3:0] Opcode,
  output [1:0] ALUop,
  output RegDest,
  output ALUsrc,
  output MemRead,
  output MemWrite,
  output MemToReg,
  output RegWrite,
  output Beq,
  output Bne,
  output Jump
);

  wire decoder_1_out1, decoder_1_out6, decoder_1_out8, decoder_1_out9, decoder_1_out10, decoder_1_out11,
       decoder_1_out12, decoder_1_out13, decoder_1_out14;

  Decoder #(.select(4), .enable("false")) decoder_1 (
    .out0(ALUop[1]), .out1(decoder_1_out1), .out2(Beq), .out3(Bne), .out4(MemWrite), .out5(Jump),
    .out6(decoder_1_out6), .out7(MemRead), .out8(decoder_1_out8), .out9(decoder_1_out9),
    .out10(decoder_1_out10), .out11(decoder_1_out11), .out12(decoder_1_out12), .out13(decoder_1_out13),
    .out14(decoder_1_out14), .sel(Opcode));  // open: out15
  or or_1 (ALUop[0], Beq, Bne);
  or or_2 (ALUsrc, decoder_1_out1, MemWrite, decoder_1_out6);
  or or_3 (RegWrite, decoder_1_out1, decoder_1_out6, ALUop[1]);

  assign MemToReg = MemRead;
  assign RegDest = ALUop[1];

  // Notes on the sheet:
  //   Figure: Main Control Unit
endmodule

module Datapath (
  input  in_1
);

  wire alu_1_zero, and_1_out, and_2_out, Clock_out, main_control_unit_1_alusrc, main_control_unit_1_beq,
       main_control_unit_1_bne, main_control_unit_1_jump, main_control_unit_1_memread,
       main_control_unit_1_memtoreg, main_control_unit_1_memwrite, main_control_unit_1_regdest,
       main_control_unit_1_regwrite, not_1_out;
  wire [1:0] main_control_unit_1_aluop;
  wire [3:0] alu_control_unit_1_alu_control_signal;
  wire [4:0] bit_extender_3_out, multiplexer_1_out;
  wire [23:0] adder_1_out, alu_1_alu_output, bit_extender_1_out, bit_extender_2_out, bit_extender_4_out,
       multiplexer_2_out, multiplexer_3_out, multiplexer_4_out, multiplexer_5_out, multiplexer_6_out, PC_q,
       ram_1_data, register_file_1_read_data_1, register_file_1_read_data_2, rom_1_data;

  Register #(.width(24)) PC (.D(multiplexer_5_out), .Q(PC_q), .clk(Clock_out));  // open: en, clr
  assign bit_extender_1_out = {{23{1'b0}}, 1'b1};  // Bit_Extender bit_extender_1
  Adder #(.width(24)) adder_1 (.a(bit_extender_1_out), .b(PC_q), .out(adder_1_out));  // open: cin, cout
  ROM #(.addrWidth(24), .dataWidth(24)) rom_1 (.addr(PC_q), .data(rom_1_data));  // open: sel
  Clock Clock (.out(Clock_out));
  assign bit_extender_2_out = {{4{1'b0}}, rom_1_data[19:0]};  // Bit_Extender bit_extender_2
  assign bit_extender_3_out = {{4{1'b0}}, rom_1_data[4]};  // Bit_Extender bit_extender_3
  Main_Control_Unit main_control_unit_1 (
    .Opcode(rom_1_data[23:20]), .ALUop(main_control_unit_1_aluop), .RegDest(main_control_unit_1_regdest),
    .ALUsrc(main_control_unit_1_alusrc), .MemRead(main_control_unit_1_memread),
    .MemWrite(main_control_unit_1_memwrite), .MemToReg(main_control_unit_1_memtoreg),
    .RegWrite(main_control_unit_1_regwrite), .Beq(main_control_unit_1_beq), .Jump(main_control_unit_1_jump),
    .Bne(main_control_unit_1_bne));
  assign bit_extender_4_out = {{14{1'b0}}, rom_1_data[9:0]};  // Bit_Extender bit_extender_4
  Multiplexer #(.width(5), .enable("false")) multiplexer_1 (
    .in0(rom_1_data[14:10]), .in1(rom_1_data[9:5]), .out(multiplexer_1_out), .sel(main_control_unit_1_regdest));
  Register_File register_file_1 (
    .Clock(Clock_out), .Read_data_1(register_file_1_read_data_1), .Read_data_2(register_file_1_read_data_2),
    .Write_register(multiplexer_1_out), .write_control(main_control_unit_1_regwrite),
    .write_data(multiplexer_6_out), .clear(in_1), .Read_register_1(rom_1_data[19:15]),
    .Read_register_2(rom_1_data[14:10]));
  ALU_Control_Unit alu_control_unit_1 (
    .Function(rom_1_data[3:0]), .ALU_Control_Signal(alu_control_unit_1_alu_control_signal),
    .ALUop(main_control_unit_1_aluop));
  Multiplexer #(.width(24), .enable("false")) multiplexer_2 (
    .in0(register_file_1_read_data_2), .in1(bit_extender_4_out), .out(multiplexer_2_out),
    .sel(main_control_unit_1_alusrc));
  and and_1 (and_1_out, main_control_unit_1_beq, alu_1_zero);
  Multiplexer #(.width(24), .enable("false")) multiplexer_3 (
    .in0(adder_1_out), .in1(bit_extender_4_out), .out(multiplexer_3_out), .sel(and_1_out));
  not not_1 (not_1_out, alu_1_zero);
  ALU alu_1 (
    .Shampt(bit_extender_3_out), .ALU_output(alu_1_alu_output), .Zero(alu_1_zero),
    .Rs(register_file_1_read_data_1), .Rt(multiplexer_2_out),
    .ALU_control_signal(alu_control_unit_1_alu_control_signal));
  Multiplexer #(.width(24), .enable("false")) multiplexer_4 (
    .in0(multiplexer_3_out), .in1(bit_extender_4_out), .out(multiplexer_4_out), .sel(and_2_out));
  and and_2 (and_2_out, main_control_unit_1_bne, not_1_out);
  Multiplexer #(.width(24), .enable("false")) multiplexer_5 (
    .in0(multiplexer_4_out), .in1(bit_extender_2_out), .out(multiplexer_5_out), .sel(main_control_unit_1_jump));
  RAM #(.addrWidth(24), .dataWidth(24), .bus("separate")) ram_1 (
    .addr(alu_1_alu_output), .din(register_file_1_read_data_2), .data(ram_1_data),
    .str(main_control_unit_1_memwrite), .clk(Clock_out), .ld(main_control_unit_1_memread));  // open: sel, clr
  Multiplexer #(.width(24), .enable("false")) multiplexer_6 (
    .in0(alu_1_alu_output), .in1(ram_1_data), .out(multiplexer_6_out), .sel(main_control_unit_1_memtoreg));

  // Notes on the sheet:
  //   contents of rom_1 (hex, n*v repeats v):
  //   600406 600804
  //   Function
  //   Shampt
  //   Rd
  //   RS
  //   Opcode
  //   Rt
  //   24-Bits Mips Datapath
  //   ALU Control Unit
endmodule
